# Fritzing sketch ElectronicCircuit (saved by Fritzing 0.9.2b)
breadboards: 4

parts:
  Composant1 = Arduino Nano (Rev3.0)
  U1 = MAX7219 [package=dil24]
  S1 = Pushbutton [package="[THT]"]
  S2 = Pushbutton [package="[THT]"]
  S3 = Pushbutton [package="[THT]"]
  S4 = Pushbutton [package="[THT]"]
  S5 = Pushbutton [package="[THT]"]
  part = Electrolytic Capacitor [capacitance=10µF voltage=25V package="100 mil [THT, electrolytic]"]
  part_2 = Ceramic Capacitor [capacitance=100nF package="100 mil [THT, multilayer]"]
  part_3 = Resistor [tolerance=±5% resistance=29k package=THT]
  Disp1 = LBT2088AH [part_number=LBT2088AH]
  LCD1 = LCD screen  # not connected
  J1 = Piezo Speaker
  I2C_Display = IC, DIP package, 4 pins [chip_label=I2C]
  I2C_RTC = IC, DIP package, 4 pins [chip_label=I2C]
  R2 = Photocell (LDR) [package=THT]
  R3 = Resistor [tolerance=±5% resistance=220 package=THT]

nets:
  N1: Composant1.D2, U1.DIN
  N2: Composant1.D3, U1.LOAD
  N3: Composant1.D4, U1.CLK
  N4: Composant1.D5, S1.Pin_3, S1.Pin_4
  N5: Composant1.D6, S2.Pin_4
  N6: Composant1.D7, S3.Pin_3, S3.Pin_4
  N7: Composant1.D8, S4.Pin_3, S4.Pin_4
  GND: Composant1.GND, U1.GND, U1.GND2, S1.Pin_1, S1.Pin_2, S2.Pin_1, S2.Pin_2, S3.Pin_1, S3.Pin_2, S4.Pin_1, S5.Pin_1, S5.Pin_2, part.+, part_2.0, J1.pin1, I2C_Display.pin2, I2C_RTC.pin2, R2.pin_1
  5V: Composant1.5V, U1.VCC, part_2.1, part_3.Pin_1, I2C_Display.pin1, I2C_RTC.pin1, R3.Pin_0
  N8: Composant1.A5, I2C_Display.pin4, I2C_RTC.pin4
  N9: Composant1.A4, I2C_Display.pin3, I2C_RTC.pin3
  N10: Composant1.A1, R2.pin_0, R3.Pin_1
  N11: Composant1.A0, J1.pin2
  N12: U1.DIG0, Disp1.pin_13
  N13: U1.DIG4, Disp1.pin_6
  N14: U1.DIG6, Disp1.pin_15
  N15: U1.DIG2, Disp1.pin_4
  N16: U1.DIG3, Disp1.pin_10
  N17: U1.DIG7, Disp1.pin_16
  N18: U1.DIG5, Disp1.pin_11
  N19: U1.DIG1, Disp1.pin_3
  N20: U1.SEGA, Disp1.pin2
  N21: U1.SEGF, Disp1.pin_14
  N22: U1.SEGB, Disp1.pin_7
  N23: U1.SEGG, Disp1.pin_9
  N24: U1.ISET, part_3.Pin_0
  N25: U1.SEGC, Disp1.pin1
  N26: U1.SEGE, Disp1.pin_8
  N27: U1.SEGDP, Disp1.pin_5
  N28: U1.SEGD, Disp1.pin_12

notes:
  The left IC is an I2C adapter for the LCD display.
  The right IC is an I2C real time clock module
  Resistances not specified, you need to choose the good values
